// Logisim project MUX.circ as structural Verilog: 3 circuits, main circuit main
module main (
  input  in_1,
  input  in_2,
  input  in_3,
  output out_4
);

  wire and_1_out, and_2_out, not_1_out;

  not not_1 (not_1_out, in_1);
  and and_1 (and_1_out, not_1_out, in_2);
  and and_2 (and_2_out, in_1, in_3);
  or or_1 (out_4, and_1_out, and_2_out);
endmodule

module _4x1MUX (
  input  in_1,
  input  in_2,
  input  in_3,
  input  in_4,
  input  in_5,
  input  in_6,
  output out_7
);

  wire and_1_out, and_2_out, and_3_out, and_4_out, not_1_out, not_2_out;

  not not_1 (not_1_out, in_1);
  not not_2 (not_2_out, in_2);
  and and_1 (and_1_out, not_2_out, not_1_out, in_3);
  and and_2 (and_2_out, in_2, not_1_out, in_4);
  and and_3 (and_3_out, not_2_out, in_1, in_5);
  and and_4 (and_4_out, in_2, in_1, in_6);
  or or_1 (out_7, and_1_out, and_2_out, and_3_out, and_4_out);
endmodule

module _1bit_LU (
);

  // NOT_Gate not_1 is placed but not wired
  // AND_Gate and_1 is placed but not wired
  // OR_Gate or_1 is placed but not wired
  // XOR_Gate xor_1 is placed but not wired
  _4x1MUX u_4x1mux_1 ();  // open: in_1, in_2, in_3, in_4, in_5, in_6, out_7
endmodule
