// Logisim project register.circ as structural Verilog: 2 circuits, main circuit SR 래치
module \SR_래치  (
  input  in_1,
  input  in_2,
  input  in_3,
  input  in_4,
  output out_5,
  output out_6,
  output out_7,
  output out_8
);

  nand nand_1 (out_5, in_1, out_6);
  nand nand_2 (out_6, out_5, in_2);
  nor nor_1 (out_7, in_3, out_8);
  nor nor_2 (out_8, out_7, in_4);
endmodule

module \게이트_SR_래치  (
  input  in_1,
  input  in_2,
  output out_3,
  output out_4
);

  nor nor_1 (out_3, in_1, out_4);
  nor nor_2 (out_4, out_3, in_2);
endmodule
